# Fritzing sketch arudino_motor_cd (saved by Fritzing 0.9.3b)
breadboards: 1

parts:
  IC1 = ULN2003A [package="DIP16 [THT]"]
  Componente1 = Arduino Uno (Rev3)
  M1 = DC Motor

nets:
  N1: IC1.In_3, Componente1.D10_PWM/SS
  N2: IC1.0V, Componente1.GND
  N3: IC1.COM_-_Common, M1.pin_2
  N4: IC1.Out_3, M1.pin_1
